// Logisim project equal.circ as structural Verilog: 1 circuit, main circuit main
module main (
  input  ms,
  input  A,
  input  ls,
  input  in_4,
  input  B,
  input  in_6,
  output Equal
);

  wire xnor_1_out, xnor_2_out, xnor_3_out;

  xnor xnor_1 (xnor_1_out, ms, in_4);
  xnor xnor_2 (xnor_2_out, A, B);
  xnor xnor_3 (xnor_3_out, ls, in_6);
  and and_1 (Equal, xnor_1_out, xnor_2_out, xnor_3_out);

  // Notes on the sheet:
  //   3 bit Equality
endmodule
